// Logisim project round.circ as structural Verilog: 1 circuit, main circuit main
module main (
  input  [7:0] Dividend,
  input  [7:0] in_2,
  input  in_3,
  output [7:0] Initial_Answer,
  output [7:0] Remainder
);

  wire adder_1_cout, comparator_1_eq, comparator_1_gt, or_1_out;
  wire [0:0] and_1_out;
  wire [7:0] adder_1_out, shifter_1_out;

  // Probe on Initial_Answer
  Divider divider_1 (.a(Dividend), .b(in_2), .out(Initial_Answer), .rem(Remainder));  // open: upper
  // Probe on in_2
  Shifter #(.shift("lr")) shifter_1 (.in(in_2), .\dist (3'b001), .out(shifter_1_out));
  // Probe on Remainder
  // Probe on shifter_1_out
  Comparator #(.mode("unsigned")) comparator_1 (
    .a(Remainder), .b(shifter_1_out), .gt(comparator_1_gt), .eq(comparator_1_eq));  // open: lt
  // Probe on or_1_out
  or or_1 (or_1_out, comparator_1_gt, comparator_1_eq);
  and and_1 (and_1_out[0], or_1_out, in_3);
  LED led_1 (.in(and_1_out[0]));
  Adder adder_1 (.a(Initial_Answer), .b({{7{1'b0}}, and_1_out[0]}), .out(adder_1_out), .cin(1'b0), .cout(adder_1_cout));
  // Probe on adder_1_out
  // Probe on adder_1_cout

  // Other names for the same wires on the sheet: B[7:0] = Initial_Answer

  // Notes on the sheet:
  //   Julia Moran
  //   Dr. Carelli
  //   September 21, 2022
  //   Divisor
  //   CSC 235 Project 1: Round
  //   Inital Answer
  //   B - Inital Answer from Divider
  //   Divisor
  //   Divides the divisor by 2 by
  //   shifting it by 1 from the right
  //   Remainder
  //   Shifted Value
  //   Indicates if the remainder
  //   is greater or equal to
  //   the shifted value
  //   Input that decides whether
  //   or not to round
  //   Indicates if rounding
  //   will occur
  //   B - Inital Answer
  //   Combine the 1 bit indication
  //   with 7 bits of 0 so it can be
  //   added to the inital answer
  //   Adds 1 to the inital answer if it
  //   needs to be rounded, reoutputs
  //   the inital truncated answer
  //   otherwise
  //   Final Answer
endmodule
