// Logisim project LEDcounter.circ as structural Verilog: 1 circuit, main circuit main
module main (
  input  [3:0] in_1
);

  wire and_1_out, and_2_out, and_3_out, and_4_out, and_5_out, and_6_out, and_7_out, and_8_out, and_9_out,
       and_10_out, and_11_out, and_12_out, and_13_out, and_14_out, and_15_out, clock_1_out, comparator_1_gt,
       comparator_2_gt, not_1_out, not_2_out, not_3_out, not_4_out, or_1_out, or_2_out, or_3_out, or_4_out,
       or_5_out, or_6_out, or_7_out;
  wire [3:0] adder_1_out, multiplexer_1_out, register_1_q;

  // Probe on register_1_q
  // Probe on register_1_q
  // Probe on adder_1_out
  Adder #(.width(4)) adder_1 (.a(register_1_q), .b(4'b0001), .out(adder_1_out), .cin(1'b0));  // open: cout
  Comparator #(.width(4), .mode("unsigned")) comparator_1 (
    .a(register_1_q), .b(4'b1000), .gt(comparator_1_gt));  // open: eq, lt
  Comparator #(.width(4), .mode("unsigned")) comparator_2 (
    .a(register_1_q), .b(in_1), .gt(comparator_2_gt));  // open: eq, lt
  or or_1 (or_1_out, comparator_1_gt, comparator_2_gt);
  // Probe on multiplexer_1_out
  Multiplexer #(.width(4), .disabled(0), .enable("false")) multiplexer_1 (
    .in0(adder_1_out), .in1(4'b0000), .out(multiplexer_1_out), .sel(or_1_out));
  Clock clock_1 (.out(clock_1_out));
  Hex_Digit_Display hex_digit_display_1 (.value(register_1_q));  // open: dp
  Register #(.width(4)) register_1 (.D(multiplexer_1_out), .Q(register_1_q), .clk(clock_1_out));  // open: en, clr
  not not_1 (not_1_out, register_1_q[3]);
  not not_2 (not_2_out, register_1_q[2]);
  not not_3 (not_3_out, register_1_q[1]);
  not not_4 (not_4_out, register_1_q[0]);
  and and_1 (and_1_out, not_2_out, register_1_q[1], register_1_q[0]);
  and and_2 (and_2_out, register_1_q[2], not_3_out, register_1_q[0]);
  and and_3 (and_3_out, not_2_out, not_3_out, not_4_out);
  and and_4 (and_4_out, register_1_q[2], not_3_out);
  and and_5 (and_5_out, register_1_q[2], not_4_out);
  and and_6 (and_6_out, not_2_out, not_3_out, not_4_out);
  and and_7 (and_7_out, not_2_out, register_1_q[1], register_1_q[0]);
  and and_8 (and_8_out, register_1_q[2], register_1_q[1], not_4_out);
  and and_9 (and_9_out, not_1_out, not_4_out);
  and and_10 (and_10_out, register_1_q[3], register_1_q[0]);
  and and_11 (and_11_out, register_1_q[2], register_1_q[1]);
  and and_12 (and_12_out, not_1_out, not_2_out, not_4_out);
  and and_13 (and_13_out, register_1_q[3], register_1_q[0]);
  and and_14 (and_14_out, register_1_q[2], register_1_q[0]);
  and and_15 (and_15_out, register_1_q[2], not_3_out);
  or or_2 (or_2_out, and_1_out, and_2_out, and_3_out, register_1_q[3]);
  or or_3 (or_3_out, and_4_out, and_5_out, register_1_q[3]);
  or or_4 (or_4_out, and_6_out, and_7_out, and_8_out, register_1_q[3]);
  or or_5 (or_5_out, and_9_out, and_10_out, and_11_out);
  or or_6 (or_6_out, register_1_q[2], register_1_q[0]);
  or or_7 (or_7_out, and_12_out, and_13_out, and_14_out, and_15_out);
  LED led_1 (.in(or_2_out));
  LED led_2 (.in(or_7_out));
  LED led_3 (.in(or_3_out));
  LED led_4 (.in(or_4_out));
  LED led_5 (.in(or_6_out));
  LED led_6 (.in(or_5_out));

  // Notes on the sheet:
  //   Julia Moran
  //   Dr. Carelli
  //   October 28, 2022
  //   User inputed
  //   maximum value
  //   CSC 235 Project 2: LED Counter
  //   Increment the value
  //   in the register by 1
  //   Value in register
  //   Compare the value in
  //   the register with 8 so
  //   that the max value is 9
  //   as default
  //   Value in register
  //   Count after it is
  //   incremented
  //   Compare the value in the
  //   register with the maximum
  //   inputed by the user
  //   Counter
  //   Value to be
  //   stored in the
  //   If the max has been
  //   reached, store the
  //   incremented value
  //   Else, reset the value
  //   in the register to 0
  //   Check if the user
  //   inputed max value
  //   or the default max
  //   value of 9 has been
  //   reached.
  //   register
  //   Clock signal
  //   Displays the count currently
  //   in the register
  //   Register
  //   A
  //   Input Bits and Complements
  //   B
  //   Decoder
  //   D
  //   C
  //   Top Left
  //   Top Center
  //   Top Right
  //   Bottom Right
  //   Bottom Center
  //   Bottom Left
  //   Output
endmodule
